# Fritzing sketch schematic (saved by Fritzing 0.9.3b)
breadboards: 1

parts:
  Part1 = Arduino Color LCD Shield
  U1 = mini DIN 6 Connector [package=mini-din6]  # not connected
  Part2 = Arduino Uno (Rev3) - ICSP

nets:
  GND: Part1.GND, Part2.GND
  5V: Part1.5V, Part2.5V
