# Fritzing sketch simon_types_schematic (saved by Fritzing 0.9.3b)
breadboards: 1

parts:
  - = Arduino Uno (Rev3) - ICSP
  -_2 = LCD screen
  -_3 = Resistor [tolerance=±5% resistance=220 package=THT]
  -_4 = Trimmer Potentiometer [maximum_resistance=10kΩ package=THT]
  -_5 = LED - 5mm [color="Green (555nm)" package="5 mm [THT]"]
  -_6 = LED - 5mm [color="Red (633nm)" package="5 mm [THT]"]
  R1 = Resistor [tolerance=±5% resistance=220 package=THT]
  R2 = Resistor [tolerance=±5% resistance=220 package=THT]
  -_7 = mini DIN 6 Connector [package=mini-din6]

nets:
  5V: -.5V, -_2.VDD, -_4.leg1, -_7.2
  GND: -.GND, -_2.VSS, -_2.R/W, -_2.LED-, -_4.leg2, -_5.cathode, -_6.cathode, -_7.6
  N1: -.D9_PWM, R1.Pin_0
  N2: -.D10_PWM/SS, R2.Pin_0
  N3: -.D11_PWM/MOSI, -_2.E
  N4: -.D12/MISO, -_2.RS
  N5: -.D3_PWM, -_7.3
  N6: -.D4, -_2.DB7
  N7: -.D5_PWM, -_2.DB6
  N8: -.D6_PWM, -_2.DB5
  N9: -.D7, -_2.DB4
  N10: -_2.V0, -_4.wiper
  N11: -_2.LED+, -_3.Pin_1
  N12: -_5.anode, R1.Pin_1
  N13: -_6.anode, R2.Pin_1

notes:
  PS2 Connector
